# Fritzing sketch Tea-dipper (saved by Fritzing 0.9.4)
breadboards: 1

parts:
  LCD1 = LCD screen
  S1 = Pushbutton [package="[SMD]"]
  S2 = Pushbutton [package="[SMD]"]
  J1 = Piezo Speaker
  R1 = Rotary Potentiometer (Small) [maximum_resistance=100kΩ package=THT]
  Part1 = Arduino Uno (Rev3)
  R2 = Resistor [tolerance=±5% resistance=10k package=THT]
  R3 = Resistor [tolerance=±5% resistance=10k package=THT]
  M1 = Dagu DGServo 9g (Pan and tilt) [part_number=RS001B]
  R4 = Resistor [tolerance=±5% resistance=220 package=THT]

nets:
  GND: LCD1.VSS, LCD1.R/W, LCD1.LED-, R1.leg2, Part1.GND, R2.Pin_1, R3.Pin_1, M1.gnd, R4.Pin_1
  VDD: LCD1.VDD, LCD1.LED+, S1.Pin_3, S1.Pin_4, S2.Pin_3, S2.Pin_4, R1.leg1, Part1.5V, M1.vcc
  N1: LCD1.V0, R1.wiper
  N2: LCD1.RS, Part1.D7
  N3: LCD1.E, Part1.D8
  N4: LCD1.DB0, Part1.D9_PWM
  N5: LCD1.DB1, Part1.D10_PWM/SS
  N6: LCD1.DB2, Part1.D11_PWM/MOSI
  N7: LCD1.DB7, Part1.D12/MISO
  N8: S1.Pin_1, S1.Pin_2, Part1.D3_PWM, R3.Pin_0
  N9: S2.Pin_1, S2.Pin_2, Part1.D2, R2.Pin_0
  N10: J1.pin1, R4.Pin_0
  N11: J1.pin2, Part1.D5_PWM
  N12: Part1.D4, M1.pulse
